// Logisim project CPU.circ as structural Verilog: 1 circuit, main circuit CPU
module CPU (
  input  Fetch,
  output out_2,
  output [9:0] out_3
);

  wire clock_1_out;
  wire [9:0] PC_p3;

  Clock clock_1 (.out(clock_1_out));
  // _10BitRegister PC: pin names not known; wires that end beside it: Fetch, clock_1_out, PC_p3, out_3
  _10BitIncrementer u_10bitincrementer_1 (.I(out_3), .S(PC_p3), .Overflow(out_2));

  // Notes on the sheet:
  //   out_3: pull=down
  //   Fetch: pull=down
endmodule
