// Logisim project ControlUnit.circ as structural Verilog: 1 circuit, main circuit Control Unit
module Control_Unit (
  input  PC_Overflow,
  input  [19:0] Inst,
  input  clk,
  output Fetch,
  output ALU_Control,
  output RegRead,
  output RegWrite,
  output MemRead,
  output MemWrite,
  output PCRead,
  output PCWrite,
  output Imm,
  output RegW_Select,
  output PCW_Select,
  output BE_Select,
  output [2:0] ALU_Select,
  output [3:0] Dr,
  output [3:0] Sr1,
  output [3:0] Sr2,
  output [19:0] Imm_Offset,
  output [9:0] Addr
);

  wire Instruction_Decoder_halt, Instruction_Decoder_jump, Instruction_Decoder_ld, Instruction_Decoder_pop,
       Instruction_Decoder_push, Instruction_Decoder_st, not_1_out, signal_generator_1_decode,
       signal_generator_1_instructionend, signal_generator_1_pop_2, signal_generator_1_push_2,
       stack_pointer_1_stack_overflow, stack_pointer_1_stackaddress, state_manager_1_s0, state_manager_1_s1,
       state_manager_1_s2, terminator_1_halted;
  wire [9:0] Instruction_Decoder_addr, stack_pointer_1_sp;
  wire [19:0] IR_q;

  _20BitRegister IR (.clk(not_1_out), .I(Inst), .Q(IR_q), .W_Enable(signal_generator_1_decode));
  not not_1 (not_1_out, signal_generator_1_decode);
  Instruction_Decoder Instruction_Decoder (
    .in_1(IR_q), .ALU_Select(ALU_Select), .ALU(RegW_Select), .IMM(Imm), .LD(Instruction_Decoder_ld),
    .ST(Instruction_Decoder_st), .PUSH(Instruction_Decoder_push), .POP(Instruction_Decoder_pop),
    .JUMP(Instruction_Decoder_jump), .BE(PCW_Select), .BE_Select(BE_Select), .HALT(Instruction_Decoder_halt),
    .DR(Dr), .SR1(Sr1), .SR2(Sr2), .IMM_2(Imm_Offset), .ADDR(Instruction_Decoder_addr));
  Stack_Pointer stack_pointer_1 (
    .clk(clk), .Pop(signal_generator_1_pop_2), .Push(signal_generator_1_push_2), .SP(stack_pointer_1_sp),
    .Stack_Overflow(stack_pointer_1_stack_overflow), .StackAddress(stack_pointer_1_stackaddress));
  State_Manager state_manager_1 (
    .ALU(RegW_Select), .LD(Instruction_Decoder_ld), .ST(Instruction_Decoder_st),
    .PUSH(Instruction_Decoder_push), .POP(Instruction_Decoder_pop), .JUMP(Instruction_Decoder_jump),
    .BE(PCW_Select), .clk(clk), .S2(state_manager_1_s2), .S1(state_manager_1_s1), .S0(state_manager_1_s0));
  Terminator terminator_1 (
    .clk(clk), .Decode(signal_generator_1_decode), .Halt_Instruction(Instruction_Decoder_halt),
    .Instruction_End(signal_generator_1_instructionend), .PC_Overflow(PC_Overflow),
    .Halted(terminator_1_halted), .Stack_Overflow(stack_pointer_1_stack_overflow));
  Multiplexer #(.width(10), .disabled(0), .enable("false")) multiplexer_1 (
    .in0(Instruction_Decoder_addr), .in1(stack_pointer_1_sp), .out(Addr), .sel(stack_pointer_1_stackaddress));
  Signal_Generator signal_generator_1 (
    .HALTED(terminator_1_halted), .InstructionEnd(signal_generator_1_instructionend), .ALU(RegW_Select),
    .LD(Instruction_Decoder_ld), .Fetch(Fetch), .ST(Instruction_Decoder_st), .PUSH(Instruction_Decoder_push),
    .POP(Instruction_Decoder_pop), .Decode(signal_generator_1_decode), .JUMP(Instruction_Decoder_jump),
    .ALUControl(ALU_Control), .BE(PCW_Select), .S2(state_manager_1_s2), .RegRead(RegRead),
    .S1(state_manager_1_s1), .S0(state_manager_1_s0), .RegWrite(RegWrite), .MemRead(MemRead),
    .MemWrite(MemWrite), .PCRead(PCRead), .PCWrite(PCWrite), .Push_2(signal_generator_1_push_2),
    .Pop_2(signal_generator_1_pop_2));

  // Notes on the sheet:
  //   PCW_Select: pull=down
  //   ALU_Control: pull=down
  //   Dr: pull=down
  //   PCRead: pull=down
  //   RegWrite: pull=down
  //   PC_Overflow: pull=down
  //   Sr1: pull=down
  //   RegRead: pull=down
  //   Imm_Offset: pull=down
  //   MemRead: pull=down
  //   Inst: pull=down
  //   BE_Select: pull=down
  //   Fetch: pull=down
  //   RegW_Select: pull=down
  //   Imm: pull=down
  //   clk: pull=down
  //   Addr: pull=down
  //   PCWrite: pull=down
  //   MemWrite: pull=down
  //   ALU_Select: pull=down
  //   Sr2: pull=down
endmodule
