// Logisim project RisingEdgeTriggeredDFlipFlop.circ as structural Verilog: 1 circuit, main circuit RisingEdgeTriggeredDFlipFlop
module RisingEdgeTriggeredDFlipFlop (
  input  D,
  input  C,
  output Q
);

  wire dlatch_1_q, not_1_out;

  not not_1 (not_1_out, C);
  DLatch dlatch_1 (.D(D), .clk(not_1_out), .Q(dlatch_1_q));
  DLatch dlatch_2 (.D(dlatch_1_q), .clk(C), .Q(Q));
endmodule
