// Logisim project Memory.circ as structural Verilog: 1 circuit, main circuit Memory
module Memory (
  input  [9:0] A,
  input  [19:0] D,
  input  C,
  input  MS,
  input  OS,
  output [19:0] D_2
);

  wire not_1_out, not_2_out;
  wire [19:0] ram_1_data, ram_2_data;

  not not_1 (not_1_out, MS);
  RAM #(.addrWidth(10), .dataWidth(20), .bus("separate")) ram_1 (
    .addr(A), .din(D), .data(ram_1_data), .str(OS), .sel(not_1_out), .clk(C), .ld(not_2_out));  // open: clr
  not not_2 (not_2_out, OS);
  _20BitBitwiseAnd u_20bitbitwiseand_1 (.I0(ram_2_data), .I1(ram_1_data), .S(D_2));
  RAM #(.addrWidth(10), .dataWidth(20), .bus("separate")) ram_2 (
    .addr(A), .din(D), .data(ram_2_data), .str(OS), .sel(MS), .clk(C), .ld(not_2_out));  // open: clr

  // Notes on the sheet:
  //   Data Memory
  //   Instruction Memory
endmodule
