// Logisim project RegisterFile.circ as structural Verilog: 1 circuit, main circuit RegisterFile
module RegisterFile (
  input  [3:0] WS,
  input  [19:0] I,
  input  C,
  input  W,
  input  [3:0] RS,
  input  [19:0] O
);

  wire and_1_out, and_2_out, and_3_out, and_4_out, and_5_out, and_6_out, and_7_out, and_8_out, and_9_out,
       and_10_out, and_11_out, and_12_out, and_13_out, and_14_out, and_15_out, and_16_out, decoder_1_out0,
       decoder_1_out1, decoder_1_out2, decoder_1_out3, decoder_1_out4, decoder_1_out5, decoder_1_out6,
       decoder_1_out7, decoder_1_out8, decoder_1_out9, decoder_1_out10, decoder_1_out11, decoder_1_out12,
       decoder_1_out13, decoder_1_out14, decoder_1_out15;
  wire [19:0] n20bitregister_1_p4, n20bitregister_2_p4, n20bitregister_3_p4, n20bitregister_4_p4,
       n20bitregister_5_p4, n20bitregister_6_p4, n20bitregister_7_p4, n20bitregister_8_p4,
       n20bitregister_9_p4, n20bitregister_10_p4, n20bitregister_11_p4, n20bitregister_12_p4,
       n20bitregister_13_p4, n20bitregister_14_p4, n20bitregister_15_p4, n20bitregister_16_p4;

  and and_1 (and_1_out, decoder_1_out0, C);
  and and_2 (and_2_out, decoder_1_out1, C);
  // _20BitRegister 20bitregister_1: pin names not known; wires that end beside it: and_1_out, W, I, n20bitregister_1_p4
  // _20BitRegister 20bitregister_2: pin names not known; wires that end beside it: and_2_out, W, I, n20bitregister_2_p4
  and and_3 (and_3_out, decoder_1_out2, C);
  and and_4 (and_4_out, decoder_1_out3, C);
  // _20BitRegister 20bitregister_3: pin names not known; wires that end beside it: and_3_out, W, I, n20bitregister_3_p4
  // _20BitRegister 20bitregister_4: pin names not known; wires that end beside it: and_4_out, W, I, n20bitregister_4_p4
  and and_5 (and_5_out, decoder_1_out4, C);
  and and_6 (and_6_out, decoder_1_out5, C);
  // _20BitRegister 20bitregister_5: pin names not known; wires that end beside it: and_5_out, W, I, n20bitregister_5_p4
  // _20BitRegister 20bitregister_6: pin names not known; wires that end beside it: and_6_out, W, I, n20bitregister_6_p4
  and and_7 (and_7_out, decoder_1_out6, C);
  and and_8 (and_8_out, decoder_1_out7, C);
  // _20BitRegister 20bitregister_7: pin names not known; wires that end beside it: and_7_out, W, I, n20bitregister_7_p4
  Decoder #(.select(4), .enable("false")) decoder_1 (
    .out0(decoder_1_out0), .out1(decoder_1_out1), .out2(decoder_1_out2), .out3(decoder_1_out3),
    .out4(decoder_1_out4), .out5(decoder_1_out5), .out6(decoder_1_out6), .out7(decoder_1_out7),
    .out8(decoder_1_out8), .out9(decoder_1_out9), .out10(decoder_1_out10), .out11(decoder_1_out11),
    .out12(decoder_1_out12), .out13(decoder_1_out13), .out14(decoder_1_out14), .out15(decoder_1_out15),
    .sel(WS));
  // _20BitRegister 20bitregister_8: pin names not known; wires that end beside it: and_8_out, W, I, n20bitregister_8_p4
  and and_9 (and_9_out, decoder_1_out8, C);
  Multiplexer #(.select(4), .width(20), .enable("false")) multiplexer_1 (
    .in0(n20bitregister_1_p4), .in1(n20bitregister_2_p4), .in2(n20bitregister_3_p4),
    .in3(n20bitregister_4_p4), .in4(n20bitregister_5_p4), .in5(n20bitregister_6_p4),
    .in6(n20bitregister_7_p4), .in7(n20bitregister_8_p4), .in8(n20bitregister_9_p4),
    .in9(n20bitregister_10_p4), .in10(n20bitregister_11_p4), .in11(n20bitregister_12_p4),
    .in12(n20bitregister_13_p4), .in13(n20bitregister_14_p4), .in14(n20bitregister_15_p4),
    .in15(n20bitregister_16_p4), .out(O), .sel(RS));
  and and_10 (and_10_out, decoder_1_out9, C);
  // _20BitRegister 20bitregister_9: pin names not known; wires that end beside it: and_9_out, W, I, n20bitregister_9_p4
  // _20BitRegister 20bitregister_10: pin names not known; wires that end beside it: and_10_out, W, I, n20bitregister_10_p4
  and and_11 (and_11_out, decoder_1_out10, C);
  and and_12 (and_12_out, decoder_1_out11, C);
  // _20BitRegister 20bitregister_11: pin names not known; wires that end beside it: and_11_out, W, I, n20bitregister_11_p4
  // _20BitRegister 20bitregister_12: pin names not known; wires that end beside it: and_12_out, W, I, n20bitregister_12_p4
  and and_13 (and_13_out, decoder_1_out12, C);
  and and_14 (and_14_out, decoder_1_out13, C);
  // _20BitRegister 20bitregister_13: pin names not known; wires that end beside it: and_13_out, W, I, n20bitregister_13_p4
  // _20BitRegister 20bitregister_14: pin names not known; wires that end beside it: and_14_out, W, I, n20bitregister_14_p4
  and and_15 (and_15_out, decoder_1_out14, C);
  and and_16 (and_16_out, decoder_1_out15, C);
  // _20BitRegister 20bitregister_15: pin names not known; wires that end beside it: and_15_out, W, I, n20bitregister_15_p4
  // _20BitRegister 20bitregister_16: pin names not known; wires that end beside it: and_16_out, W, I, n20bitregister_16_p4
endmodule
